// Logisim project CPU_t3.circ as structural Verilog: 5 circuits, main circuit main
module main (
  input  [31:0] in_1
);

  wire buzzer_1_p3, CLK, keyboard_1_avail, not_1_out, not_2_out, undriven;
  wire [23:0] buzzer_1_p1;
  wire [31:0] keyboard_1_data;

  Clock clock_1 (.out(CLK));
  CPU cpu_1 ();  // open: CLK, inData, inAddress, outData, outAddress, R_W, debIR_out, debAdrReg, debPC, debSP, debMDR, debFlagReg
  Hex_Digit_Display hex_digit_display_1 (.value(in_1[31:28]));  // open: dp
  Hex_Digit_Display hex_digit_display_2 (.value(in_1[27:24]));  // open: dp
  Hex_Digit_Display hex_digit_display_3 (.value(in_1[23:20]));  // open: dp
  Hex_Digit_Display hex_digit_display_4 (.value(in_1[19:16]));  // open: dp
  Hex_Digit_Display hex_digit_display_5 (.value(in_1[15:12]));  // open: dp
  Hex_Digit_Display hex_digit_display_6 (.value(in_1[11:8]));  // open: dp
  Hex_Digit_Display hex_digit_display_7 (.value(in_1[7:4]));  // open: dp
  Hex_Digit_Display hex_digit_display_8 (.value(in_1[3:0]));  // open: dp
  not not_1 (not_1_out, buzzer_1_p3);
  Decoder #(.select(3)) decoder_1 ();  // open: out0, out1, out2, out3, out4, out5, out6, out7, sel, en
  Keyboard keyboard_1 (
    .clk(CLK), .re(buzzer_1_p3), .clr(undriven), .avail(keyboard_1_avail), .data(keyboard_1_data[6:0]));
  RAM #(.addrWidth(20), .dataWidth(32)) ram_1 (
    .addr(buzzer_1_p1[19:0]), .we(buzzer_1_p3), .oe(not_1_out), .clk(CLK), .din(keyboard_1_data),
    .dout(keyboard_1_data));
  TTY #(.cols(120), .rows(48)) tty_1 ();  // open: data, clk, we, clr
  // Buzzer buzzer_1: pin names not known; wires that end beside it: buzzer_1_p1, keyboard_1_data, buzzer_1_p3, keyboard_1_data
  not not_2 (not_2_out, buzzer_1_p3);
  RAM #(.addrWidth(16), .dataWidth(32)) ram_2 (
    .addr(buzzer_1_p1[15:0]), .we(buzzer_1_p3), .oe(not_2_out), .clk(CLK), .din(keyboard_1_data),
    .dout(keyboard_1_data));
  ROM #(.addrWidth(24)) rom_1 (.addr(buzzer_1_p1), .data(keyboard_1_data[7:0]));
  // RGB_Video #(.height(256), .scale(8), .width(256)) rgb_video_1: pin names not known; wires that end beside it: CLK, buzzer_1_p3, keyboard_1_data, keyboard_1_data, keyboard_1_data
  // Pins of 2 and 16 and 20 and 24 bits meet at buzzer_1_p1
  // Pins of 7 and 8 and 32 bits meet at keyboard_1_data
endmodule

module CPU (
  input  CLK,
  input  [31:0] inData,
  input  [31:0] inAddress,
  output outData,
  output [31:0] outAddress,
  output R_W,
  output debIR_out,
  output debAdrReg,
  output debPC,
  output debSP,
  output debMDR,
  output debFlagReg
);

  wire ADR_out, ADR_we, and_1_out, comparator_1_eq, comparator_1_gt, comparator_1_lt, MDR_out, MDR_we,
       or_1_out, undriven_2, undriven_4, undriven_5, undriven_6, undriven_7, undriven_8, undriven_9,
       undriven_10;
  wire [1:0] undriven, undriven_3;
  wire [4:0] FlagRegister_q, undriven_11;
  wire [7:0] adder_1_out, demultiplexer_1_out0, demultiplexer_1_out1, StackRegister_q;
  wire [31:0] ACC_q, AddressRegister_q, alu_1_alu_out, controlled_buffer_1_out, controlled_buffer_2_out,
       InstructionRegister_q, MDR_q, multiplexer_1_out, ProgramCounter_q, registerfile_1_regout, TEMP_q;

  Register #(.width(32)) MDR (.D(inData), .en(MDR_we), .clk(CLK), .Q(MDR_q));  // open: clr
  Register #(.width(32)) AddressRegister (.D(inAddress), .en(ADR_we), .clk(CLK), .Q(AddressRegister_q));  // open: clr
  assign controlled_buffer_1_out = MDR_out ? MDR_q : 32'bz;  // Controlled_Buffer controlled_buffer_1
  assign controlled_buffer_2_out = ADR_out ? AddressRegister_q : 32'bz;  // Controlled_Buffer controlled_buffer_2
  RegisterFile registerfile_1 (
    .CLK(CLK), .inData(controlled_buffer_1_out), .REG_inSel(undriven), .WE(undriven_2),
    .REG_outSel(undriven_3), .OUT_enb(undriven_4), .regOut(registerfile_1_regout));
  assign controlled_buffer_1_out = undriven_5 ? registerfile_1_regout : 32'bz;  // Controlled_Buffer controlled_buffer_3
  Register #(.width(32)) TEMP (.D(registerfile_1_regout), .clk(CLK), .Q(TEMP_q));  // open: en, clr
  Register #(.width(32)) InstructionRegister (
    .D(controlled_buffer_1_out), .en(undriven_6), .clk(CLK), .Q(InstructionRegister_q));  // open: clr
  Multiplexer #(.width(32)) multiplexer_1 (
    .in0(registerfile_1_regout), .in1(controlled_buffer_1_out), .out(multiplexer_1_out));  // open: sel
  ALU alu_1 (.inA(TEMP_q), .inB(multiplexer_1_out), .ALU_out(alu_1_alu_out));  // open: ShiftAmount
  ControlUnit controlunit_1 ();  // open: CLK, IR_in, controlBits
  Demultiplexer #(.width(8)) demultiplexer_1 (
    .out0(demultiplexer_1_out0), .out1(demultiplexer_1_out1), .in(StackRegister_q));  // open: sel
  Adder adder_1 (.a(demultiplexer_1_out0), .b({8{1'b1}}), .out(adder_1_out));  // open: cin, cout
  Subtractor subtractor_1 (.a(demultiplexer_1_out1), .b({8{1'b1}}), .out(adder_1_out));  // open: bin, bout
  and and_1 (and_1_out, undriven_7, or_1_out);
  or or_1 (or_1_out, undriven_8, undriven_9);
  Register #(.width(32)) ACC (.D(alu_1_alu_out), .clk(CLK), .Q(ACC_q));  // open: en, clr
  Counter #(.max('hffffffff), .width(32)) ProgramCounter (
    .Q(ProgramCounter_q), .clk(CLK));  // open: load, D, count, carry, up, clr
  Register StackRegister (.D(adder_1_out), .Q(StackRegister_q));  // open: en, clk, clr
  Multiplexer #(.width(32)) multiplexer_2 (
    .in0(ProgramCounter_q), .in1(controlled_buffer_2_out), .out(outAddress), .sel(undriven_10));
  Comparator #(.width(32)) comparator_1 (
    .a(ACC_q), .gt(comparator_1_gt), .eq(comparator_1_eq), .lt(comparator_1_lt));  // open: b
  Register #(.width(5)) FlagRegister (.D(undriven_11), .clk(CLK), .Q(FlagRegister_q));  // open: en, clr

  // Notes on the sheet:
  //   I3B
  //   I3B
  //   carry
  //   Flagreg
  //   flagReg.m_carry
endmodule

module ALU (
  input  [31:0] inA,
  input  [31:0] inB,
  input  [4:0] ShiftAmount,
  output [31:0] ALU_out
);

  wire adder_1_cout, subtractor_1_bout, undriven, undriven_2;
  wire [31:0] adder_1_out, and_1_out, not_1_out, or_1_out, shifter_1_out, shifter_2_out, subtractor_1_out,
       xor_1_out;

  Adder #(.width(32)) adder_1 (.a(inA), .b(inB), .out(adder_1_out), .cin(undriven), .cout(adder_1_cout));
  Subtractor #(.width(32)) subtractor_1 (
    .a(inA), .b(inB), .out(subtractor_1_out), .bin(undriven_2), .bout(subtractor_1_bout));
  Multiplier #(.width(32)) multiplier_1 ();  // open: a, b, out, cin, cout
  Divider divider_1 ();  // open: a, b, out, upper, rem
  Comparator comparator_1 ();  // open: a, b, gt, eq, lt
  Shifter #(.width(32)) shifter_1 (.in(inA), .\dist (ShiftAmount), .out(shifter_1_out));
  Shifter #(.shift("lr"), .width(32)) shifter_2 (.in(inA), .\dist (ShiftAmount), .out(shifter_2_out));
  assign and_1_out = inA & inB;  // AND_Gate and_1, 32 bits wide
  assign not_1_out = ~inA;  // NOT_Gate not_1, 32 bits wide
  assign or_1_out = inA | inB;  // OR_Gate or_1, 32 bits wide
  assign xor_1_out = inA ^ inB;  // XOR_Gate xor_1, 32 bits wide
  Multiplexer #(.select(4), .width(32)) multiplexer_1 (.out(ALU_out));  // open: in0, in1, in2, in3, in4, in5, in6, in7, in8, in9, in10, in11, in12, in13, in14, in15, sel

  // Notes on the sheet:
  //   2s comp
endmodule

module RegisterFile (
  input  CLK,
  input  [31:0] inData,
  input  [1:0] REG_inSel,
  input  WE,
  input  [1:0] REG_outSel,
  input  OUT_enb,
  output [31:0] regOut
);

  wire demultiplexer_2_out0, demultiplexer_2_out1, demultiplexer_2_out2, demultiplexer_2_out3;
  wire [31:0] demultiplexer_1_out0, demultiplexer_1_out1, demultiplexer_1_out2, demultiplexer_1_out3, reg0_q,
       reg1_q, reg2_q, reg3_q;

  Demultiplexer #(.select(2), .width(32)) demultiplexer_1 (
    .out0(demultiplexer_1_out0), .out1(demultiplexer_1_out1), .out2(demultiplexer_1_out2),
    .out3(demultiplexer_1_out3), .in(inData), .sel(REG_inSel));
  Demultiplexer #(.select(2)) demultiplexer_2 (
    .out0(demultiplexer_2_out0), .out1(demultiplexer_2_out1), .out2(demultiplexer_2_out2),
    .out3(demultiplexer_2_out3), .in(WE), .sel(REG_inSel));
  Register #(.width(32)) reg0 (
    .D(demultiplexer_1_out0), .en(demultiplexer_2_out0), .clk(CLK), .Q(reg0_q));  // open: clr
  Register #(.width(32)) reg1 (
    .D(demultiplexer_1_out1), .en(demultiplexer_2_out1), .clk(CLK), .Q(reg1_q));  // open: clr
  Register #(.width(32)) reg2 (
    .D(demultiplexer_1_out2), .en(demultiplexer_2_out2), .clk(CLK), .Q(reg2_q));  // open: clr
  Register #(.width(32)) reg3 (
    .D(demultiplexer_1_out3), .en(demultiplexer_2_out3), .clk(CLK), .Q(reg3_q));  // open: clr
  Multiplexer #(.enable("true"), .select(2), .width(32)) multiplexer_1 (
    .in0(reg0_q), .in1(reg1_q), .in2(reg2_q), .in3(reg3_q), .out(regOut), .sel(REG_outSel), .en(OUT_enb));
endmodule

module ControlUnit (
  input  CLK,
  input  [31:0] IR_in,
  output [15:0] controlBits
);

  wire decoder_1_out4;
  wire [3:0] counter_1_q;
  wire [7:0] counter_2_q, rom_1_data;

  ROM rom_1 (.addr(IR_in[31:24]), .data(rom_1_data));
  Decoder #(.enable("false"), .select(4)) decoder_1 (
    .out4(decoder_1_out4), .sel(counter_1_q));  // open: out0, out1, out2, out3, out5, out6, out7, out8, out9, out10, out11, out12, out13, out14, out15
  Counter #(.max('hf), .width(4)) counter_1 (.Q(counter_1_q), .clk(CLK));  // open: load, D, count, carry, up, clr
  Counter counter_2 (.D(rom_1_data), .Q(counter_2_q), .clk(CLK));  // open: load, count, carry, up, clr
  ROM #(.dataWidth(16)) rom_2 (.addr(counter_2_q), .data(controlBits));
endmodule
